# Fritzing sketch S000_LED-Basic-Circuit (saved by Fritzing 0.6.5b)
breadboards: 1

parts:
  U1 = atmega168 [package="DIP28 [THT]"]
  J1 = female pin header, 6 pins [form="♀ (female)"]
  C1 = Ceramic Capacitor [capacitance=10pF package="100 mil [THT, multilayer]"]
  R1 = Resistor [tolerance=±5% resistance=220 package=THT]
  R2 = Resistor [tolerance=±5% resistance=1k package=THT]
  LED1 = LED - 5mm [color="Red (633nm)" package="5 mm [THT]"]
  S1 = Pushbutton [package="[THT]"]

nets:
  N1: U1.Pin_1, C1.0, R1.Pin_1
  N2: U1.Pin_2, J1.pin4
  N3: U1.Pin_3, J1.pin5
  N4: U1.Pin_7, J1.pin3, R1.Pin_0
  N5: U1.Pin_8, U1.Pin_22, J1.pin1, LED1.cathode, S1.Pin_1, S1.Pin_2
  N6: U1.Pin_18, S1.Pin_3, S1.Pin_4
  N7: U1.Pin_19, R2.Pin_0
  N8: J1.pin6, C1.1
  N9: R2.Pin_1, LED1.anode
