# Fritzing sketch schema (saved by Fritzing 0.6.3b)
breadboards: 1

parts:
  U1 = atmega168 [package="DIP28 [THT]"]
  J1 = female pin header, 6 pins [form="♀ (female)"]
  C1 = Tantalum Capacitor [capacitance=100nF package="100 mil [THT, tantalum]"]
  R1 = Resistor [tolerance=±5% resistance=10k package=THT]
  R2 = Resistor [tolerance=±5% resistance=470 package=THT]
  LED1 = LED - 5mm [color="Green (555nm)" package="5 mm [THT]"]
  VCC1 = 4 x AAA Battery Mount
  S1 = Pushbutton [package="[THT]"]
  R3 = Resistor [tolerance=±5% resistance=330 package=THT]
  LED2 = LED - 5mm [color="Red (633nm)" package="5 mm [THT]"]
  R4 = Resistor [tolerance=±5% resistance=330 package=THT]
  R5 = Resistor [tolerance=±5% resistance=330 package=THT]
  LED3 = LED - 5mm [color="Red (633nm)" package="5 mm [THT]"]
  LED4 = LED - 5mm [color="Red (633nm)" package="5 mm [THT]"]

nets:
  N1: U1.Pin_1, C1.+, R1.Pin_1
  N2: U1.Pin_2, J1.pin4
  N3: U1.Pin_3, J1.pin5
  N4: U1.Pin_6, U1.Pin_15
  N5: U1.Pin_7, U1.Pin_20, J1.pin3, R1.Pin_0, VCC1.+
  N6: U1.Pin_8, U1.Pin_22, J1.pin1, LED1.cathode, VCC1.-, S1.Pin_1, S1.Pin_2, LED2.cathode, LED3.cathode, LED4.cathode
  N7: U1.Pin_14, S1.Pin_3, S1.Pin_4
  N8: U1.Pin_16, R5.Pin_0
  N9: U1.Pin_17, R4.Pin_0
  N10: U1.Pin_18, R3.Pin_0
  N11: U1.Pin_19, R2.Pin_0
  N12: J1.pin6, C1.-
  N13: R2.Pin_1, LED1.anode
  N14: R3.Pin_1, LED2.anode
  N15: R4.Pin_1, LED3.anode
  N16: R5.Pin_1, LED4.anode

notes:
  Power must not exceed 5V!
  The power device is only symbolic to satisfy the circuit drawing and PCB.
  Here you plug in your
  Spurkfun "5V FTDI Basic" for programming. Your may used it to power yout circuit as well
  SCL
  SDA
